// Logisim project (a)-Logic.circ as structural Verilog: 1 circuit, main circuit main
module main (
  input  _1a,
  input  _2b,
  input  _3c,
  input  _4d
);

  wire and_1_out, and_2_out, and_3_out, and_4_out, not_1_out, not_2_out, not_3_out, not_4_out, or_1_out;

  not not_1 (not_1_out, _1a);
  not not_2 (not_2_out, _2b);
  not not_3 (not_3_out, _3c);
  not not_4 (not_4_out, _4d);
  and and_1 (and_1_out, _4d, not_2_out, not_3_out, not_1_out);
  and and_2 (and_2_out, not_1_out, not_3_out, _2b, not_4_out);
  and and_3 (and_3_out, _4d, not_2_out, _3c, _4d);
  and and_4 (and_4_out, _4d, _2b, not_3_out, _4d);
  or or_1 (or_1_out, and_1_out, and_2_out, and_3_out, and_4_out);
  LED led_1 (.in(or_1_out));

  // Notes on the sheet:
  //   (a)
endmodule
