// Logisim project (b)-Logic.circ as structural Verilog: 1 circuit, main circuit main
module main (
  input  _1a,
  input  _2b,
  input  _3c,
  input  _4d
);

  wire and_1_out, and_2_out, and_3_out, and_4_out, and_5_out, and_6_out, not_1_out, not_2_out, not_3_out,
       not_4_out, or_1_out, or_2_out, or_3_out;

  not not_1 (not_1_out, _1a);
  not not_2 (not_2_out, _2b);
  not not_3 (not_3_out, _3c);
  not not_4 (not_4_out, _4d);
  and and_1 (and_1_out, not_1_out, _2b, not_3_out, not_4_out);
  and and_2 (and_2_out, _1a, not_2_out, not_3_out, _4d);
  and and_3 (and_3_out, _1a, not_2_out, _3c, _4d);
  and and_4 (and_4_out, _1a, _2b, not_3_out, not_4_out, not_4_out);
  and and_5 (and_5_out, _4d, _1a, _2b, _3c);
  and and_6 (and_6_out, _1a, _2b, _3c, not_4_out);
  or or_1 (or_1_out, and_1_out, and_2_out, and_3_out);
  or or_2 (or_2_out, and_4_out, and_5_out, and_6_out);
  LED led_1 (.in(or_3_out));
  or or_3 (or_3_out, or_1_out, or_2_out);

  // Notes on the sheet:
  //   (b)
endmodule
